# Fritzing sketch ESQUEMA (saved by Fritzing 0.9.10b)
circuit board: 6.95208cm x 5.54398cm
breadboards: 1

parts:
  Mod1 = KY-022 Infrared Receiver Module [package="Breakout board"]
  LED1 = LED - 5mm [color="Red (633nm)" current=0.030 package="5 mm [THT]"]
  J1 = Basic Servo
  HC-SR04_Sensor_1 = HC-SR04 Ultrasonic Distance Sensor
  Componente1 = Arduino Uno (Rev3)

nets (from the breadboard view):
  GND: Mod1.-, LED1.cathode, J1.gnd, HC-SR04_Sensor_1.GND, Componente1.GND
  VCC: Mod1.Vin, J1.vcc, HC-SR04_Sensor_1.VCC, Componente1.5V
  N1: Mod1.S, Componente1.D11_PWM/MOSI
  N2: LED1.anode, Componente1.D5_PWM
  N3: J1.pulse, Componente1.D8
  N4: HC-SR04_Sensor_1.TRIG, Componente1.D7
  N5: HC-SR04_Sensor_1.ECHO, Componente1.D6_PWM

custom parts:
  KY-022 Infrared Receiver Module: KY-022 IR receiver module, reacts to 38kHz infrared light.
